// Logisim project regfile.circ as structural Verilog: 1 circuit, main circuit regfile
module regfile (
  input  [4:0] ReadIndex1,
  input  [4:0] ReadIndex2,
  input  [4:0] WriteIndex,
  input  [31:0] WriteData,
  input  RegWEn,
  input  clk,
  output [31:0] ra,
  output [31:0] sp,
  output [31:0] t0,
  output [31:0] t1,
  output [31:0] t2,
  output [31:0] s0,
  output [31:0] s1,
  output [31:0] a0,
  output [31:0] ReadData1,
  output [31:0] ReadData2
);

  wire clock_1_out, clock_2_out, clock_3_out, clock_4_out, clock_5_out, clock_6_out, clock_7_out,
       clock_8_out, clock_9_out, clock_10_out, clock_11_out, clock_12_out, clock_13_out, clock_14_out,
       clock_15_out, clock_16_out, clock_17_out, clock_18_out, W, W1;
  wire [7:0] x3, x6, x7, x8, x9, x10, x11, x12, x13, x14, x15, x16, x17, x18;
  wire [31:0] write_data, x4, x5;

  Clock clock_1 (.out(clock_1_out));
  Clock clock_2 (.out(clock_2_out));
  Clock clock_3 (.out(clock_3_out));
  Clock clock_4 (.out(clock_4_out));
  Clock clock_5 (.out(clock_5_out));
  Clock clock_6 (.out(clock_6_out));
  Register #(.width(32)) register_1 (.D(write_data), .en(W1), .clk(clock_1_out), .Q(ra));  // open: clr
  Register register_2 (.D(write_data[7:0]), .en(W), .clk(clock_2_out), .Q(sp[7:0]));  // open: clr
  Register #(.width(32)) register_3 (.D(write_data), .en(W1), .clk(clock_5_out), .Q(x5));  // open: clr
  Register register_4 (.D(write_data[7:0]), .en(W1), .clk(clock_3_out), .Q(x3));  // open: clr
  Register #(.width(32)) register_5 (.D(write_data), .en(W1), .clk(clock_4_out), .Q(x4));  // open: clr
  Register register_6 (.D(write_data[7:0]), .en(W1), .clk(clock_6_out), .Q(x6));  // open: clr
  Clock clock_7 (.out(clock_7_out));
  Clock clock_8 (.out(clock_8_out));
  Clock clock_9 (.out(clock_9_out));
  Clock clock_10 (.out(clock_10_out));
  Clock clock_11 (.out(clock_11_out));
  Clock clock_12 (.out(clock_12_out));
  Register register_7 (.D(write_data[7:0]), .en(W1), .clk(clock_7_out), .Q(x7));  // open: clr
  Register register_8 (.D(write_data[7:0]), .en(W1), .clk(clock_8_out), .Q(x8));  // open: clr
  Register register_9 (.D(write_data[7:0]), .en(W1), .clk(clock_9_out), .Q(x9));  // open: clr
  Register register_10 (.D(write_data[7:0]), .en(W1), .clk(clock_10_out), .Q(x10));  // open: clr
  Register register_11 (.D(write_data[7:0]), .en(W1), .clk(clock_11_out), .Q(x11));  // open: clr
  Register register_12 (.D(write_data[7:0]), .en(W1), .clk(clock_12_out), .Q(x12));  // open: clr
  Clock clock_13 (.out(clock_13_out));
  Clock clock_14 (.out(clock_14_out));
  Clock clock_15 (.out(clock_15_out));
  Clock clock_16 (.out(clock_16_out));
  Clock clock_17 (.out(clock_17_out));
  Clock clock_18 (.out(clock_18_out));
  Register register_13 (.D(write_data[7:0]), .en(W1), .clk(clock_17_out), .Q(x13));  // open: clr
  Register register_14 (.D(write_data[7:0]), .en(W1), .clk(clock_18_out), .Q(x14));  // open: clr
  Register register_15 (.D(write_data[7:0]), .en(W1), .clk(clock_13_out), .Q(x15));  // open: clr
  Register register_16 (.D(write_data[7:0]), .en(W1), .clk(clock_14_out), .Q(x16));  // open: clr
  Register register_17 (.D(write_data[7:0]), .en(W1), .clk(clock_15_out), .Q(x17));  // open: clr
  Register register_18 (.D(write_data[7:0]), .en(W1), .clk(clock_16_out), .Q(x18));  // open: clr
  // Pins of 8 and 32 bits meet at write_data
  // Pins of 8 and 32 bits meet at sp
  // Pins of 8 and 32 bits meet at x5
  // Pins of 8 and 32 bits meet at x4

  // Other names for the same wires on the sheet: x1[31:0] = ra; x2[31:0] = sp

  // Notes on the sheet:
  //   INPUTS to your circuit
  //   DON'T CHANGE THE LOCATIONS OF THE INPUTS AND OUTPUTS!
  //   These are DEBUG/TEST outputs from your circuit.
  //   OUTPUTS from your circuit
endmodule
